// Logisim project Alu.circ as structural Verilog: 7 circuits, main circuit ALU FINAL
module ALU_8_bit (
  input  InvB,
  input  [1:0] OP,
  input  QR,
  input  A0,
  input  B0,
  input  A1,
  input  B1,
  input  A2,
  input  B2,
  input  A3,
  input  B3,
  input  A4,
  input  B4,
  input  A5,
  input  B5,
  input  A6,
  input  B6,
  input  A7,
  input  B7,
  output S0,
  output S1,
  output S2,
  output S3,
  output Zero,
  output S4,
  output S5,
  output S6,
  output S7,
  output OF
);

  wire alui_1_r, alui_2_r, alui_3_r, alui_4_r, alui_5_r, alui_6_r, alui_7_r, alui_of_1_r;

  ALUi alui_1 (.InvB(InvB), .QR(QR), .A(A0), .B(B0), .L(alui_of_1_r), .S(S0), .R(alui_1_r), .OP(OP));
  ALUi alui_2 (.InvB(InvB), .QR(alui_1_r), .A(A1), .B(B1), .L(1'b0), .S(S1), .R(alui_2_r), .OP(OP));
  ALUi alui_3 (.InvB(InvB), .QR(alui_2_r), .A(A2), .B(B2), .L(1'b0), .S(S2), .R(alui_3_r), .OP(OP));
  ALUi alui_4 (.InvB(InvB), .QR(alui_3_r), .A(A3), .B(B3), .L(1'b0), .S(S3), .R(alui_4_r), .OP(OP));
  ALUi alui_5 (.InvB(InvB), .QR(alui_4_r), .A(A4), .B(B4), .L(1'b0), .S(S4), .R(alui_5_r), .OP(OP));
  ALUi alui_6 (.InvB(InvB), .QR(alui_5_r), .A(A5), .B(B5), .L(1'b0), .S(S5), .R(alui_6_r), .OP(OP));
  ALUi alui_7 (.InvB(InvB), .QR(alui_6_r), .A(A6), .B(B6), .L(1'b0), .S(S6), .R(alui_7_r), .OP(OP));
  ALUi_OF alui_of_1 (
    .InvB(InvB), .QR(alui_7_r), .A(A7), .B(B7), .L(1'b0), .S(S7), .R(alui_of_1_r), .out_9(OF), .OP(OP));
  or or_1 (Zero, S0, S1, S2, S3, S4, S5, S6, S7);
endmodule

module HA (
  input  A,
  input  B,
  output S,
  output R
);

  xor xor_1 (S, A, B);
  and and_1 (R, A, B);
endmodule

module FA (
  input  QR,
  input  A,
  input  B,
  output S,
  output R
);

  wire ha_1_r, ha_1_s, ha_2_r;

  HA ha_1 (.A(A), .B(B), .S(ha_1_s), .R(ha_1_r));
  HA ha_2 (.A(QR), .B(ha_1_s), .S(S), .R(ha_2_r));
  or or_1 (R, ha_2_r, ha_1_r);
endmodule

module OF (
  input  QR,
  input  A,
  input  B,
  output OF
);

  wire and_1_out, and_2_out;

  and and_1 (and_1_out, ~QR, A, B);  // AND_Gate
  and and_2 (and_2_out, QR, ~A, ~B);  // AND_Gate
  or or_1 (OF, and_1_out, and_2_out);
endmodule

module ALUi (
  input  InvB,
  input  QR,
  input  [1:0] OP,
  input  A,
  input  B,
  input  L,
  output S,
  output R
);

  wire and_1_out, fa_1_s, multiplexer_1_out, not_1_out, or_1_out;

  Multiplexer #(.enable("false")) multiplexer_1 (.in0(B), .in1(not_1_out), .out(multiplexer_1_out), .sel(InvB));
  not not_1 (not_1_out, B);
  and and_1 (and_1_out, A, multiplexer_1_out);
  or or_1 (or_1_out, A, multiplexer_1_out);
  FA fa_1 (.QR(QR), .A(A), .B(multiplexer_1_out), .S(fa_1_s), .R(R));
  Multiplexer #(.select(2), .enable("false")) multiplexer_2 (
    .in0(and_1_out), .in1(or_1_out), .in2(fa_1_s), .in3(L), .out(S), .sel(OP));
endmodule

module ALUi_OF (
  input  InvB,
  input  QR,
  input  [1:0] OP,
  input  A,
  input  B,
  input  L,
  output S,
  output R,
  output out_9
);

  wire and_1_out, fa_1_s, multiplexer_1_out, not_1_out, or_1_out;

  Multiplexer #(.enable("false")) multiplexer_1 (.in0(B), .in1(not_1_out), .out(multiplexer_1_out), .sel(InvB));
  not not_1 (not_1_out, B);
  and and_1 (and_1_out, A, multiplexer_1_out);
  or or_1 (or_1_out, A, multiplexer_1_out);
  FA fa_1 (.QR(QR), .A(A), .B(multiplexer_1_out), .S(fa_1_s), .R(R));
  Multiplexer #(.select(2), .enable("false")) multiplexer_2 (
    .in0(and_1_out), .in1(or_1_out), .in2(fa_1_s), .in3(L), .out(S), .sel(OP));
  OF of_1 (.QR(R), .A(A), .B(multiplexer_1_out), .OF(out_9));
endmodule

module ALU_FINAL (
  input  [7:0] A,
  input  InvB,
  input  QR,
  input  [1:0] OP,
  input  [7:0] B,
  output Zero,
  output OverFlow
);

  wire [3:0] alu_8_bit_1_s0, alu_8_bit_1_s4;

  Hex_Digit_Display hex_digit_display_1 (.value(alu_8_bit_1_s4), .dp(1'b0));
  ALU_8_bit alu_8_bit_1 (
    .InvB(InvB), .QR(QR), .A0(A[0]), .B0(B[0]), .A1(A[1]), .B1(B[1]), .A2(A[2]), .B2(B[2]), .A3(A[3]),
    .B3(B[3]), .A4(A[4]), .B4(B[4]), .A5(A[5]), .B5(B[5]), .A6(A[6]), .B6(B[6]), .A7(A[7]), .B7(B[7]),
    .S0(alu_8_bit_1_s0[0]), .S1(alu_8_bit_1_s0[1]), .S2(alu_8_bit_1_s0[2]), .S3(alu_8_bit_1_s0[3]),
    .S4(alu_8_bit_1_s4[0]), .S5(alu_8_bit_1_s4[1]), .S6(alu_8_bit_1_s4[2]), .S7(alu_8_bit_1_s4[3]),
    .OF(OverFlow), .OP(OP), .Zero(Zero));
  Hex_Digit_Display hex_digit_display_2 (.value(alu_8_bit_1_s0), .dp(1'b0));
endmodule
