// Logisim project RoadToAlu.circ as structural Verilog: 6 circuits, main circuit ALU 8 bit
module HalfAdder (
  input  A1,
  input  B1,
  output Y1,
  output Y2
);

  and and_1 (Y2, A1, B1);
  xor xor_1 (Y1, A1, B1);
endmodule

module Full_Adder (
  input  QuaryResult,
  input  A1,
  input  B1,
  output Y1,
  output Y2
);

  wire halfadder_1_y1, halfadder_1_y2, halfadder_2_y2;

  HalfAdder halfadder_1 (.A1(A1), .B1(B1), .Y1(halfadder_1_y1), .Y2(halfadder_1_y2));
  HalfAdder halfadder_2 (.A1(halfadder_1_y1), .B1(QuaryResult), .Y1(Y1), .Y2(halfadder_2_y2));
  or or_1 (Y2, halfadder_2_y2, halfadder_1_y2);
endmodule

module Adder_7b_7b (
  input  A1,
  input  B1,
  input  A2,
  input  B2,
  input  A4,
  input  B4,
  input  A8,
  input  B8,
  input  A16,
  input  B16,
  input  A32,
  input  B32,
  input  A64,
  input  B64,
  output Y1,
  output Y2,
  output Y4,
  output Y8,
  output Y16,
  output Y32,
  output Y64,
  output Y128
);

  wire full_adder_1_y2, full_adder_2_y2, full_adder_3_y2, full_adder_4_y2, full_adder_5_y2, halfadder_1_y2;

  HalfAdder halfadder_1 (.A1(A1), .B1(B1), .Y1(Y1), .Y2(halfadder_1_y2));
  Full_Adder full_adder_1 (.A1(A2), .B1(B2), .QuaryResult(halfadder_1_y2), .Y1(Y2), .Y2(full_adder_1_y2));
  Full_Adder full_adder_2 (.A1(A4), .B1(B4), .QuaryResult(full_adder_1_y2), .Y1(Y4), .Y2(full_adder_2_y2));
  Full_Adder full_adder_3 (.A1(A8), .B1(B8), .QuaryResult(full_adder_2_y2), .Y1(Y8), .Y2(full_adder_3_y2));
  Full_Adder full_adder_4 (.A1(A16), .B1(B16), .QuaryResult(full_adder_3_y2), .Y1(Y16), .Y2(full_adder_4_y2));
  Full_Adder full_adder_5 (.A1(A32), .B1(B32), .QuaryResult(full_adder_4_y2), .Y1(Y32), .Y2(full_adder_5_y2));
  Full_Adder full_adder_6 (.A1(A64), .B1(B64), .QuaryResult(full_adder_5_y2), .Y1(Y64), .Y2(Y128));
  Hex_Digit_Display hex_digit_display_1 (.value({Y128, Y64, Y32, Y16}), .dp(1'b0));
  Hex_Digit_Display hex_digit_display_2 (.value({Y8, Y4, Y2, Y1}), .dp(1'b0));
endmodule

module ALUi (
  input  OP2,
  input  OP1,
  input  QueryResult,
  input  A1,
  input  B1,
  input  L,
  output Y2,
  output Y1
);

  wire and_1_out, and_2_out, AND_3_out, and_4_out, and_5_out, and_6_out, FA_out, full_adder_1_y1, not_1_out,
       not_2_out, not_3_out, not_4_out, or_1_out, OR_2_out, QR_out;

  Full_Adder full_adder_1 (.A1(A1), .B1(B1), .QuaryResult(QueryResult), .Y1(full_adder_1_y1), .Y2(Y2));
  and and_1 (and_1_out, A1, B1);
  or or_1 (or_1_out, A1, B1);
  not not_1 (not_1_out, OP1);
  and OR_2 (OR_2_out, OP2, not_1_out);
  and QR (QR_out, OP2, OP1);
  and and_2 (and_2_out, QR_out, L);
  not not_2 (not_2_out, OP2);
  not not_3 (not_3_out, OP2);
  not not_4 (not_4_out, OP1);
  and FA (FA_out, not_2_out, not_4_out);
  and AND_3 (AND_3_out, not_3_out, OP1);
  and and_4 (and_4_out, AND_3_out, and_1_out);
  and and_5 (and_5_out, OR_2_out, or_1_out);
  and and_6 (and_6_out, FA_out, full_adder_1_y1);
  or or_3 (Y1, and_6_out, and_4_out, and_5_out, and_2_out);
endmodule

module ALUi_w_MUX (
  input  [1:0] OP,
  input  QueryResult,
  input  A1,
  input  B1,
  input  L,
  output Y1,
  output Y2
);

  wire and_1_out, full_adder_1_y1, or_1_out;

  Full_Adder full_adder_1 (.A1(A1), .B1(B1), .QuaryResult(QueryResult), .Y1(full_adder_1_y1), .Y2(Y2));
  and and_1 (and_1_out, A1, B1);
  or or_1 (or_1_out, A1, B1);
  Multiplexer #(.select(2), .enable("false")) multiplexer_1 (
    .in0(full_adder_1_y1), .in1(and_1_out), .in2(or_1_out), .in3(L), .out(Y1), .sel(OP));

  // Notes on the sheet:
  //   00 - FA
  //   01 - AND
  //   10 - OR
  //   11 - L
endmodule

// ALU
module ALU_8_bit (
  input  A7,
  input  A6,
  input  A5,
  input  A4,
  input  A3,
  input  A2,
  input  A1,
  input  A0,
  input  B7,
  input  B6,
  input  B5,
  input  B4,
  input  B3,
  input  B2,
  input  B1,
  input  B0,
  input  L,
  input  QueryResult,
  input  [1:0] OP,
  output Y8,
  output Y7,
  output Y6,
  output Y5,
  output Y4,
  output Y3,
  output Y2,
  output Y1,
  output Y0
);

  wire alui_w_mux_2_y2, alui_w_mux_3_y2, alui_w_mux_4_y2, alui_w_mux_5_y2, alui_w_mux_6_y2, alui_w_mux_7_y2,
       alui_w_mux_8_y2;

  ALUi_w_MUX alui_w_mux_1 (.QueryResult(alui_w_mux_2_y2), .A1(A7), .B1(B7), .L(L), .Y2(Y8), .Y1(Y7), .OP(OP));
  ALUi_w_MUX alui_w_mux_2 (
    .QueryResult(alui_w_mux_3_y2), .A1(A6), .B1(B6), .L(L), .Y2(alui_w_mux_2_y2), .Y1(Y6), .OP(OP));
  ALUi_w_MUX alui_w_mux_3 (
    .QueryResult(alui_w_mux_4_y2), .A1(A5), .B1(B5), .L(L), .Y2(alui_w_mux_3_y2), .Y1(Y5), .OP(OP));
  ALUi_w_MUX alui_w_mux_4 (
    .QueryResult(alui_w_mux_5_y2), .A1(A4), .B1(B4), .L(L), .Y2(alui_w_mux_4_y2), .Y1(Y4), .OP(OP));
  ALUi_w_MUX alui_w_mux_5 (
    .QueryResult(alui_w_mux_7_y2), .A1(A3), .B1(B3), .L(L), .Y2(alui_w_mux_5_y2), .Y1(Y3), .OP(OP));
  ALUi_w_MUX alui_w_mux_6 (
    .QueryResult(alui_w_mux_8_y2), .A1(A1), .B1(B1), .L(L), .Y2(alui_w_mux_6_y2), .Y1(Y1), .OP(OP));
  ALUi_w_MUX alui_w_mux_7 (
    .QueryResult(alui_w_mux_6_y2), .A1(A2), .B1(B2), .L(L), .Y2(alui_w_mux_7_y2), .Y1(Y2), .OP(OP));
  ALUi_w_MUX alui_w_mux_8 (.QueryResult(QueryResult), .A1(A0), .B1(B0), .L(L), .Y2(alui_w_mux_8_y2), .Y1(Y0), .OP(OP));

  // Notes on the sheet:
  //   00 - FA
  //   01 - AND
  //   10 - OR
  //   11 - L
endmodule
