// Logisim project 6-12-2017 - Scheda in classe.circ as structural Verilog: 5 circuits, main circuit 5 - Display 7 segmenti
module _5___Display_7_segmenti (
  input  [3:0] in_1
);

  wire decoder_1_out0, decoder_1_out1, decoder_1_out2, decoder_1_out3, decoder_1_out4, decoder_1_out5,
       decoder_1_out6, decoder_1_out7, decoder_1_out8, decoder_1_out9, decoder_1_out10, decoder_1_out11,
       decoder_1_out12, decoder_1_out13, decoder_1_out14, decoder_1_out15, or_1_out, or_2_out, or_3_out,
       or_4_out, or_5_out, or_6_out, or_7_out;

  Decoder #(.select(4), .enable("false")) decoder_1 (
    .out0(decoder_1_out0), .out1(decoder_1_out1), .out2(decoder_1_out2), .out3(decoder_1_out3),
    .out4(decoder_1_out4), .out5(decoder_1_out5), .out6(decoder_1_out6), .out7(decoder_1_out7),
    .out8(decoder_1_out8), .out9(decoder_1_out9), .out10(decoder_1_out10), .out11(decoder_1_out11),
    .out12(decoder_1_out12), .out13(decoder_1_out13), .out14(decoder_1_out14), .out15(decoder_1_out15),
    .sel(in_1));
  or or_1 (or_1_out, decoder_1_out2, decoder_1_out3, decoder_1_out4, decoder_1_out5, decoder_1_out6, decoder_1_out8, decoder_1_out9, decoder_1_out10, decoder_1_out11, decoder_1_out13, decoder_1_out14, decoder_1_out15);
  or or_2 (or_2_out, decoder_1_out0, decoder_1_out4, decoder_1_out5, decoder_1_out6, decoder_1_out8, decoder_1_out9, decoder_1_out10, decoder_1_out11, decoder_1_out12, decoder_1_out13, decoder_1_out14, decoder_1_out15);
  or or_3 (or_3_out, decoder_1_out0, decoder_1_out2, decoder_1_out3, decoder_1_out5, decoder_1_out6, decoder_1_out7, decoder_1_out8, decoder_1_out9, decoder_1_out10, decoder_1_out12, decoder_1_out14, decoder_1_out15);
  or or_4 (or_4_out, decoder_1_out0, decoder_1_out1, decoder_1_out2, decoder_1_out3, decoder_1_out4, decoder_1_out7, decoder_1_out8, decoder_1_out9, decoder_1_out10);
  _7_Segment_Display u_7_segment_display_1 (
    .g(or_1_out), .f(or_2_out), .a(or_3_out), .b(or_4_out), .e(or_5_out), .d(or_6_out), .c(or_7_out),
    .dp(1'b0));
  or or_5 (or_5_out, decoder_1_out0, decoder_1_out2, decoder_1_out6, decoder_1_out8, decoder_1_out10, decoder_1_out11, decoder_1_out12, decoder_1_out13, decoder_1_out14, decoder_1_out15);
  or or_6 (or_6_out, decoder_1_out0, decoder_1_out2, decoder_1_out3, decoder_1_out5, decoder_1_out6, decoder_1_out8, decoder_1_out9, decoder_1_out11, decoder_1_out12, decoder_1_out13, decoder_1_out14);
  or or_7 (or_7_out, decoder_1_out0, decoder_1_out1, decoder_1_out3, decoder_1_out4, decoder_1_out5, decoder_1_out6, decoder_1_out7, decoder_1_out8, decoder_1_out9, decoder_1_out10, decoder_1_out11, decoder_1_out13);
  Hex_Digit_Display hex_digit_display_1 (.value(in_1), .dp(1'b0));
endmodule

module _4___HalfAdder (
  input  A,
  input  B,
  output S,
  output R
);

  xor xor_1 (S, A, B);
  and and_1 (R, A, B);
endmodule

module _2___FullAdder (
  input  A,
  input  B,
  input  C,
  output S,
  output R
);

  wire n4_halfadder_1_r, n4_halfadder_1_s, n4_halfadder_2_r;

  _4___HalfAdder u_4_halfadder_1 (.A(A), .B(B), .S(n4_halfadder_1_s), .R(n4_halfadder_1_r));
  _4___HalfAdder u_4_halfadder_2 (.A(n4_halfadder_1_s), .B(C), .S(S), .R(n4_halfadder_2_r));
  or or_1 (R, n4_halfadder_2_r, n4_halfadder_1_r);
endmodule

module _3___Criptatore__1 (
  input  A,
  input  B,
  output X,
  output Y,
  output OF
);

  wire n4_halfadder_1_r;

  _4___HalfAdder u_4_halfadder_1 (.A(1'b1), .B(A), .S(X), .R(n4_halfadder_1_r));
  _4___HalfAdder u_4_halfadder_2 (.A(n4_halfadder_1_r), .B(B), .S(Y), .R(OF));
endmodule

module _1___Minimo_2 (
  input  A,
  input  B,
  input  C,
  output Y
);

  wire n2_fulladder_1_s;

  LED led_1 (.in(n2_fulladder_1_s));
  _2___FullAdder u_2_fulladder_1 (.A(A), .B(B), .C(C), .S(n2_fulladder_1_s), .R(Y));
endmodule
