// Logisim project Combinatorio.circ as structural Verilog
module combinatorio (
  input  [7:0] in_1,
  output out_2
);

  wire and_1_out, and_2_out, and_3_out, and_4_out, not_1_out, not_2_out, not_3_out, not_4_out, not_5_out,
       not_6_out, not_7_out, not_8_out, not_9_out, not_10_out, not_11_out, not_12_out, not_13_out,
       not_14_out, not_15_out, not_16_out, not_17_out, not_18_out, not_19_out, not_20_out;

  not not_1 (not_1_out, in_1[7]);
  not not_2 (not_2_out, in_1[5]);
  not not_3 (not_3_out, in_1[4]);
  not not_4 (not_4_out, in_1[3]);
  not not_5 (not_5_out, in_1[2]);
  not not_6 (not_6_out, in_1[7]);
  not not_7 (not_7_out, in_1[4]);
  not not_8 (not_8_out, in_1[3]);
  not not_9 (not_9_out, in_1[1]);
  not not_10 (not_10_out, in_1[0]);
  not not_11 (not_11_out, in_1[7]);
  not not_12 (not_12_out, in_1[6]);
  not not_13 (not_13_out, in_1[5]);
  not not_14 (not_14_out, in_1[2]);
  not not_15 (not_15_out, in_1[1]);
  not not_16 (not_16_out, in_1[7]);
  not not_17 (not_17_out, in_1[6]);
  not not_18 (not_18_out, in_1[3]);
  not not_19 (not_19_out, in_1[2]);
  not not_20 (not_20_out, in_1[0]);
  and and_1 (and_1_out, not_1_out, in_1[6], not_2_out, not_3_out, not_4_out, not_5_out, in_1[1], in_1[0]);
  and and_2 (and_2_out, not_6_out, in_1[6], in_1[5], not_7_out, not_8_out, in_1[2], not_9_out, not_10_out);
  and and_3 (and_3_out, not_11_out, not_12_out, not_13_out, in_1[4], in_1[3], not_14_out, not_15_out, in_1[0]);
  and and_4 (and_4_out, not_16_out, not_17_out, in_1[5], in_1[4], not_18_out, not_19_out, in_1[1], not_20_out);
  or or_1 (out_2, and_1_out, and_2_out, and_3_out, and_4_out);
endmodule

module Mux_a_8_bit (
  input  in_1,
  input  in_2,
  input  in_3,
  input  in_4,
  input  in_5,
  input  in_6,
  input  in_7,
  input  in_8,
  input  [2:0] in_9,
  output out_10
);

  wire multiplexer_1_out, multiplexer_2_out;

  Multiplexer #(.select(2), .enable("false")) multiplexer_1 (
    .in0(in_1), .in1(in_2), .in2(in_3), .in3(in_4), .out(multiplexer_1_out), .sel(in_9[1:0]));
  Multiplexer #(.select(2), .enable("false")) multiplexer_2 (
    .in0(in_5), .in1(in_6), .in2(in_7), .in3(in_8), .out(multiplexer_2_out), .sel(in_9[1:0]));
  Multiplexer #(.enable("false")) multiplexer_3 (
    .in0(multiplexer_1_out), .in1(multiplexer_2_out), .out(out_10), .sel(in_9[2]));
endmodule

module Trasposizione_di_codice (
  input  [3:0] in_1,
  input  [3:0] in_2,
  input  [3:0] in_3,
  output [3:0] out_4,
  output [3:0] Con_logica,
  output [3:0] out_6
);

  wire and_1_out, and_2_out, and_3_out, and_4_out, and_5_out, and_6_out, and_7_out, and_8_out, and_9_out,
       and_10_out, and_11_out, and_12_out, and_13_out, and_14_out, not_1_out, not_2_out, not_3_out,
       not_4_out, not_5_out, not_6_out, not_7_out, not_8_out, not_9_out, not_10_out, not_11_out, not_12_out,
       not_13_out, not_14_out, not_15_out, not_16_out, not_17_out, not_18_out, not_19_out, not_20_out,
       not_21_out, not_22_out, or_1_out;

  not not_1 (not_1_out, in_1[2]);
  and and_1 (and_1_out, in_1[3], not_1_out, not_2_out, not_3_out);
  not not_2 (not_2_out, in_1[1]);
  not not_3 (not_3_out, in_1[0]);
  not not_4 (not_4_out, in_1[3]);
  and and_2 (and_2_out, not_4_out, in_1[2], not_5_out, not_6_out);
  not not_5 (not_5_out, in_1[1]);
  not not_6 (not_6_out, in_1[0]);
  not not_7 (not_7_out, in_2[2]);
  and and_3 (and_3_out, in_2[3], not_7_out, not_8_out, not_9_out);
  not not_8 (not_8_out, in_2[1]);
  not not_9 (not_9_out, in_2[0]);
  not not_10 (not_10_out, in_2[3]);
  and and_4 (and_4_out, not_10_out, in_2[2], not_11_out, not_12_out);
  not not_11 (not_11_out, in_2[1]);
  not not_12 (not_12_out, in_2[0]);
  not not_13 (not_13_out, in_3[0]);
  and and_5 (and_5_out, not_13_out, in_3[1], in_3[2]);
  and and_6 (and_6_out, in_3[0], in_3[1], in_3[2]);
  and and_7 (and_7_out, in_3[0], not_14_out, in_3[2]);
  not not_14 (not_14_out, in_3[1]);
  not not_15 (not_15_out, in_3[0]);
  and and_8 (and_8_out, not_15_out, not_16_out, in_3[3]);
  not not_16 (not_16_out, in_3[1]);
  not not_17 (not_17_out, and_2_out);
  and and_9 (and_9_out, not_17_out, in_1[2]);
  and and_10 (and_10_out, in_1[3], not_18_out);
  not not_18 (not_18_out, and_1_out);
  Multiplexer #(.width(4), .enable("false")) multiplexer_1 (
    .in0(in_2), .in1({in_2[2], in_2[3], in_2[1:0]}), .out(Con_logica), .sel(or_1_out));
  or or_1 (or_1_out, and_3_out, and_4_out);
  or or_2 (out_6[2], and_5_out, and_6_out, and_7_out, and_8_out);
  or or_3 (out_4[2], and_1_out, and_9_out);
  or or_4 (out_4[3], and_10_out, and_2_out);
  not not_19 (not_19_out, in_3[0]);
  and and_11 (and_11_out, not_19_out, in_3[1], in_3[3]);
  and and_12 (and_12_out, in_3[0], in_3[1], in_3[3]);
  and and_13 (and_13_out, in_3[0], not_20_out, in_3[3]);
  not not_20 (not_20_out, in_3[1]);
  not not_21 (not_21_out, in_3[0]);
  and and_14 (and_14_out, not_21_out, not_22_out, in_3[2]);
  not not_22 (not_22_out, in_3[1]);
  or or_5 (out_6[3], and_11_out, and_12_out, and_13_out, and_14_out);

  assign out_4[1:0] = in_1[1:0];
  assign out_6[1:0] = in_3[1:0];

  // Notes on the sheet:
  //   Con minini temini
  //   Con Karnaugh
endmodule

module Trasposizione_di_codice__6_3 (
  input  [3:0] in_1,
  input  [3:0] in_2,
  output [3:0] out_3,
  output [3:0] out_4
);

  wire and_1_out, and_2_out, and_3_out, and_4_out, and_5_out, and_6_out, and_7_out, and_8_out, not_1_out,
       not_2_out, not_3_out, not_4_out, or_1_out;

  not not_1 (not_1_out, in_1[3]);
  not not_2 (not_2_out, in_1[0]);
  not not_3 (not_3_out, in_1[3]);
  not not_4 (not_4_out, in_1[2]);
  and and_1 (and_1_out, ~in_2[1], in_2[0]);  // AND_Gate
  and and_2 (and_2_out, in_2[3], in_2[1], in_2[0]);
  and and_3 (and_3_out, ~in_2[3], in_2[2], in_2[1]);  // AND_Gate
  and and_4 (and_4_out, in_2[3], in_2[2]);
  and and_5 (and_5_out, in_2[3], ~in_2[2], ~in_2[1]);  // AND_Gate
  and and_6 (and_6_out, ~in_2[3], in_2[1], in_2[0]);  // AND_Gate
  and and_7 (and_7_out, not_1_out, in_1[2], in_1[1], not_2_out);
  and and_8 (and_8_out, not_3_out, not_4_out, in_1[1], in_1[0]);
  or or_1 (or_1_out, and_7_out, and_8_out);
  or or_2 (out_4[0], and_1_out, and_2_out, and_3_out);
  or or_3 (out_4[2], and_4_out, and_5_out, and_6_out);
  Multiplexer #(.width(4), .enable("false")) multiplexer_1 (
    .in0(in_1), .in1({in_1[3], in_1[0], in_1[1], in_1[2]}), .out(out_3), .sel(or_1_out));

  assign {out_4[3], out_4[1]} = {in_2[3], in_2[1]};
endmodule
