// Logisim project Serbatoio.circ as structural Verilog: 3 circuits, main circuit main
module main (
  input  [1:0] Livello,
  input  [1:0] Temperatura,
  output Scarica,
  output Calda,
  output Fredda
);

  wire serbatoio_1_errore;
  wire [8:0] decoder_1_out_2;

  Decoder decoder_1 (.in_1({Temperatura, Livello}), .out_2(decoder_1_out_2));
  DotMatrix #(.inputtype("row"), .matrixcols(3), .matrixrows(3)) dotmatrix_1 (
    .row0(decoder_1_out_2[2:0]), .row1(decoder_1_out_2[5:3]), .row2(decoder_1_out_2[8:6]));
  LED led_1 (.in(serbatoio_1_errore));
  Serbatoio serbatoio_1 (
    .in_1(Livello), .in_2(Temperatura), .Fredda(Fredda), .Calda(Calda), .Scarica(Scarica),
    .Errore(serbatoio_1_errore));
endmodule

module Serbatoio (
  input  [1:0] in_1,
  input  [1:0] in_2,
  output Errore,
  output Fredda,
  output Calda,
  output Scarica
);

  wire and_3_out, and_4_out, and_5_out, nor_1_out, nor_2_out;

  and and_1 (Fredda, ~in_1[0], in_1[1], in_2[0]);  // AND_Gate
  and and_2 (Calda, ~in_1[0], in_1[1], in_2[1]);  // AND_Gate
  and and_3 (and_3_out, in_1[0], ~in_1[1], in_2[0]);  // AND_Gate
  and and_4 (and_4_out, in_1[0], ~in_2[0], in_2[1]);  // AND_Gate
  or or_1 (Scarica, and_3_out, and_4_out, and_5_out);
  nor nor_1 (nor_1_out, in_1[0], in_1[1]);
  nor nor_2 (nor_2_out, in_2[0], in_2[1]);
  and and_5 (and_5_out, in_1[0], in_2[0], ~in_2[1]);  // AND_Gate
  or or_2 (Errore, nor_1_out, nor_2_out);
endmodule

module Decoder (
  input  [3:0] in_1,
  output [8:0] out_2
);

  and and_1 (out_2[0], ~in_1[1], in_1[0], in_1[2], ~in_1[3]);  // AND_Gate
  and and_2 (out_2[1], ~in_1[1], in_1[0], in_1[2], in_1[3]);  // AND_Gate
  and and_3 (out_2[2], ~in_1[1], in_1[0], ~in_1[2], in_1[3]);  // AND_Gate
  and and_4 (out_2[3], in_1[1], in_1[0], in_1[2], ~in_1[3]);  // AND_Gate
  and and_5 (out_2[5], in_1[1], in_1[0], ~in_1[2], in_1[3]);  // AND_Gate
  and and_6 (out_2[4], in_1[1], in_1[0], in_1[2], in_1[3]);
  and and_7 (out_2[6], in_1[1], ~in_1[0], in_1[2], ~in_1[3]);  // AND_Gate
  and and_8 (out_2[7], in_1[1], ~in_1[0], in_1[2], in_1[3]);  // AND_Gate
  and and_9 (out_2[8], in_1[1], ~in_1[0], ~in_1[2], in_1[3]);  // AND_Gate
endmodule
